// Logisim project contador.circ as structural Verilog: 1 circuit, main circuit main
module main (
  input  in_1
);

  wire and_1_out, and_2_out, and_3_out, and_4_out, and_5_out, clock_1_out, d_ff_1_q, d_ff_2_q, d_ff_3_q,
       d_ff_4_q, d_ff_5_q, not_1_out;

  Clock clock_1 (.out(clock_1_out));
  and and_1 (and_1_out, in_1, not_1_out);
  D_Flip_Flop d_ff_1 (.clk(clock_1_out), .D(and_1_out), .Q(d_ff_1_q));  // open: Qn, preset, en, reset
  LED led_1 (.in(d_ff_1_q));
  D_Flip_Flop d_ff_2 (.clk(clock_1_out), .D(and_2_out), .Q(d_ff_2_q));  // open: Qn, preset, en, reset
  buf and_2 (and_2_out, d_ff_1_q);  // AND_Gate
  LED led_2 (.in(d_ff_2_q));
  D_Flip_Flop d_ff_3 (.clk(clock_1_out), .D(and_3_out), .Q(d_ff_3_q));  // open: Qn, preset, en, reset
  buf and_3 (and_3_out, d_ff_2_q);  // AND_Gate
  buf and_4 (and_4_out, d_ff_3_q);  // AND_Gate
  LED led_3 (.in(d_ff_3_q));
  D_Flip_Flop d_ff_4 (.clk(clock_1_out), .D(and_4_out), .Q(d_ff_4_q));  // open: Qn, preset, en, reset
  LED led_4 (.in(d_ff_4_q));
  buf and_5 (and_5_out, d_ff_4_q);  // AND_Gate
  D_Flip_Flop d_ff_5 (.clk(clock_1_out), .D(and_5_out), .Q(d_ff_5_q));  // open: Qn, preset, en, reset
  LED led_5 (.in(d_ff_5_q));
  not not_1 (not_1_out, d_ff_5_q);
endmodule
