// Logisim project inverter.circ as structural Verilog: 1 circuit, main circuit main
module main (
  input  in_1,
  input  in_2,
  input  in_3,
  input  in_4,
  input  in_5
);

  wire and_1_out, and_2_out, and_3_out, and_4_out, and_5_out, and_6_out, and_7_out, clock_1_out, d_ff_1_q,
       d_ff_2_q, d_ff_3_q, d_ff_4_q, not_1_out, or_1_out, or_2_out, or_3_out;

  not not_1 (not_1_out, in_5);
  Clock clock_1 (.out(clock_1_out));
  and and_1 (and_1_out, in_1, not_1_out);
  and and_2 (and_2_out, d_ff_1_q, in_5);
  D_Flip_Flop d_ff_1 (.clk(clock_1_out), .D(and_1_out), .Q(d_ff_1_q));  // open: Qn, preset, en, reset
  and and_3 (and_3_out, in_2, not_1_out);
  or or_1 (or_1_out, and_2_out, and_2_out, and_3_out);
  D_Flip_Flop d_ff_2 (.clk(clock_1_out), .D(or_1_out), .Q(d_ff_2_q));  // open: Qn, preset, en, reset
  and and_4 (and_4_out, d_ff_2_q, in_5);
  and and_5 (and_5_out, in_3, not_1_out);
  or or_2 (or_2_out, and_4_out, and_5_out);
  D_Flip_Flop d_ff_3 (.clk(clock_1_out), .D(or_2_out), .Q(d_ff_3_q));  // open: Qn, preset, en, reset
  and and_6 (and_6_out, d_ff_3_q, in_5);
  and and_7 (and_7_out, in_4, not_1_out);
  or or_3 (or_3_out, and_6_out, and_7_out);
  D_Flip_Flop d_ff_4 (.clk(clock_1_out), .D(or_3_out), .Q(d_ff_4_q));  // open: Qn, preset, en, reset
  LED led_1 (.in(d_ff_4_q));
endmodule
