// Logisim project codigo morse.circ as structural Verilog: 1 circuit, main circuit main
module main (
  input  in_1,
  input  in_2,
  input  in_3,
  input  in_4,
  input  in_5,
  input  in_6,
  input  in_7,
  input  in_8,
  input  in_9,
  input  in_10,
  output out_11,
  output out_12,
  output out_13,
  output out_14,
  output out_15,
  output out_16,
  output out_17,
  output out_18,
  output out_19,
  output out_20,
  output out_21,
  output out_22,
  output out_23,
  output out_24,
  output out_25,
  output out_26,
  output out_27,
  output out_28,
  output out_29,
  output out_30
);

  not not_1 (out_11, in_1);
  not not_2 (out_13, in_2);
  not not_3 (out_15, in_3);
  not not_4 (out_17, in_4);
  not not_5 (out_19, in_5);
  not not_6 (out_21, in_6);
  not not_7 (out_23, in_7);
  not not_8 (out_25, in_8);
  not not_9 (out_27, in_9);
  not not_10 (out_29, in_10);
  not not_11 (out_12, out_11);
  not not_12 (out_14, out_13);
  not not_13 (out_16, out_15);
  not not_14 (out_18, out_17);
  not not_15 (out_20, out_19);
  not not_16 (out_22, out_21);
  not not_17 (out_24, out_23);
  not not_18 (out_26, out_25);
  not not_19 (out_28, out_27);
  not not_20 (out_30, out_29);
endmodule
